// Logisim project BRM.circ as structural Verilog: 3 circuits, main circuit brm0
module brm0 (
  input  [15:0] OperationCode,
  input  [15:0] Operand,
  input  Clock,
  input  [15:0] ProgramCounter,
  output [15:0] RX,
  output [15:0] RY,
  output [15:0] ProgramCounterOUT,
  output ProgramCounterSET
);

  wire CALC, dcode_1_a, dcode_1_b, dcode_1_c, dcode_1_d, dcode_1_e, dcode_1_f, dcode_1_g, dcode_1_h,
       dcode_3_e, dcode_3_f, dcode_3_g, dcode_3_h, dcode_4_b, dcode_4_c, dcode_4_d, dcode_4_e, dcode_4_f,
       dcode_4_g, EAT, JMPB, JMPI, JMPO, LDX, LDY, LXY, MoveYtoX, NOP, or_4_out, SERVE, Served, SetPC, SRVI,
       SWP, Write, WriteToX, WriteToY;
  wire [3:0] bit_extender_1_out;
  wire [15:0] adder_2_out, Cal0, Cal1, Cal2, Cal3, Cal4, Cal5, Cal6, dcode_2_checkcarry,
       dcode_2_comparedcarry, DISH, Food, multiplexer_1_out, multiplexer_2_out, multiplexer_4_out,
       multiplexer_5_out, multiplexer_6_out, multiplexer_7_out, multiplexer_8_out, multiplexer_10_out,
       multiplexer_12_out, Result, subtractor_2_out, undriven, undriven_2, WriteValueX, WriteValueY;

  dCode dcode_1 (
    .Compared(undriven), .Check(undriven_2), .A(dcode_1_a), .B(dcode_1_b), .C(dcode_1_c), .D(dcode_1_d),
    .E(dcode_1_e), .F(dcode_1_f), .G(dcode_1_g), .H(dcode_1_h));  // open: ComparedCarry, CheckCarry
  Bit_Extender #(.in_width(16), .out_width(4), .\type ("zero")) bit_extender_1 (.in(RY), .out(bit_extender_1_out));
  assign Cal6 = ~RX;  // NOT_Gate not_1, 16 bits wide
  Adder #(.width(16)) adder_1 (.a(RX), .b(RY), .out(Cal0));  // open: cin, cout
  Subtractor #(.width(16)) subtractor_1 (.a(RX), .b(RY), .out(Cal1));  // open: bin, bout
  Multiplier #(.width(16)) multiplier_1 (.a(RX), .b(RY), .out(Cal2));  // open: cin, cout
  Shifter #(.width(16)) shifter_1 (.in(RX), .\dist (bit_extender_1_out), .out(Cal3));
  assign Cal4 = RX & RY;  // AND_Gate and_1, 16 bits wide
  assign Cal5 = RX | RY;  // OR_Gate or_1, 16 bits wide
  Adder #(.width(16)) adder_2 (.a(ProgramCounter), .b(Operand), .out(adder_2_out));  // open: cin, cout
  Register #(.width(16)) X (.D(WriteValueX), .en(WriteToX), .Q(RX), .clk(Clock), .clr(1'b0));
  Subtractor #(.width(16)) subtractor_2 (.a(ProgramCounter), .b(Operand), .out(subtractor_2_out));  // open: bin, bout
  dCode dcode_2 (
    .Compared(OperationCode), .Check({16{1'b0}}), .ComparedCarry(dcode_2_comparedcarry),
    .CheckCarry(dcode_2_checkcarry), .A(LDX), .B(LDY), .C(SWP), .D(LXY), .E(SERVE), .F(EAT), .G(NOP), .H(CALC));
  dCode dcode_3 (
    .Compared(dcode_2_comparedcarry), .Check(dcode_2_checkcarry), .A(SRVI), .B(JMPI), .C(JMPO), .D(JMPB),
    .E(dcode_3_e), .F(dcode_3_f), .G(dcode_3_g), .H(dcode_3_h));  // open: ComparedCarry, CheckCarry
  Multiplexer #(.width(16)) multiplexer_1 (.in0({16{1'b0}}), .in1(Operand), .out(multiplexer_1_out), .sel(JMPI));
  Multiplexer #(.width(16)) multiplexer_2 (
    .in0(multiplexer_1_out), .in1(adder_2_out), .out(multiplexer_2_out), .sel(JMPO));
  Register #(.width(16)) Y (.D(WriteValueY), .en(WriteToY), .Q(RY), .clk(Clock), .clr(1'b0));
  Multiplexer #(.width(16)) multiplexer_3 (
    .in0(multiplexer_2_out), .in1(subtractor_2_out), .out(ProgramCounterOUT), .sel(JMPB));
  dCode dcode_4 (
    .Compared(DISH), .Check({16{1'b0}}), .B(dcode_4_b), .C(dcode_4_c), .D(dcode_4_d), .E(dcode_4_e),
    .F(dcode_4_f), .G(dcode_4_g));  // open: ComparedCarry, CheckCarry, A, H
  or or_2 (SetPC, JMPI, JMPO, JMPB);
  Multiplexer #(.width(16)) multiplexer_4 (.in0(Cal0), .in1(Cal1), .out(multiplexer_4_out), .sel(dcode_4_b));
  Multiplexer #(.width(16)) multiplexer_5 (
    .in0(multiplexer_4_out), .in1(Cal2), .out(multiplexer_5_out), .sel(dcode_4_c));
  Multiplexer #(.width(16)) multiplexer_6 (
    .in0(multiplexer_5_out), .in1(Cal3), .out(multiplexer_6_out), .sel(dcode_4_d));
  Register #(.width(16)) u_Dish (.D(Food), .en(SERVE), .Q(DISH), .clk(Clock), .clr(1'b0));
  or or_3 (MoveYtoX, LXY, SWP);
  Multiplexer #(.width(16)) multiplexer_7 (
    .in0(multiplexer_6_out), .in1(Cal4), .out(multiplexer_7_out), .sel(dcode_4_e));
  Multiplexer #(.width(16)) multiplexer_8 (
    .in0(multiplexer_7_out), .in1(Cal5), .out(multiplexer_8_out), .sel(dcode_4_f));
  or or_4 (or_4_out, EAT, CALC);
  Multiplexer #(.width(16)) multiplexer_9 (.in0(multiplexer_8_out), .in1(Cal6), .out(Result), .sel(dcode_4_g));
  Multiplexer #(.width(16)) multiplexer_10 (.in0(Operand), .in1(RY), .out(multiplexer_10_out), .sel(MoveYtoX));
  Multiplexer #(.width(16)) multiplexer_11 (.in0(Operand), .in1(RX), .out(WriteValueY), .sel(SWP));
  or or_5 (WriteToX, LDX, or_4_out, MoveYtoX);
  or or_6 (WriteToY, LDY, SWP);
  or or_7 (Write, WriteToX, WriteToY);
  Multiplexer #(.width(16)) multiplexer_12 (.in0(multiplexer_10_out), .in1(DISH), .out(multiplexer_12_out), .sel(EAT));
  Multiplexer #(.width(16)) multiplexer_13 (.in0(multiplexer_12_out), .in1(Result), .out(WriteValueX), .sel(CALC));
  Multiplexer #(.width(16)) multiplexer_14 (.in0(RX), .in1(Operand), .out(Food), .sel(SRVI));
  or or_8 (Served, SERVE, SRVI);
  and and_2 (ProgramCounterSET, SetPC, Clock);

  // Other names for the same wires on the sheet: OPCODE[15:0] = OperationCode; PC[15:0] = ProgramCounter;
  //   PCOUT[15:0] = ProgramCounterOUT

  // Notes on the sheet:
  //   dont touch
endmodule

module dCode (
  input  [15:0] Compared,
  input  [15:0] Check,
  output A,
  output B,
  output C,
  output D,
  output E,
  output F,
  output G,
  output H,
  output [15:0] ComparedCarry,
  output [15:0] CheckCarry
);

  wire [15:0] adder_1_out, adder_2_out, adder_3_out, adder_4_out, adder_5_out, adder_6_out, adder_7_out;

  Adder #(.width(16)) adder_1 (.a(16'h1), .b(Check), .out(adder_1_out));  // open: cin, cout
  Adder #(.width(16)) adder_2 (.a(16'h1), .b(adder_1_out), .out(adder_2_out));  // open: cin, cout
  Adder #(.width(16)) adder_3 (.a(16'h1), .b(adder_2_out), .out(adder_3_out));  // open: cin, cout
  Adder #(.width(16)) adder_4 (.a(16'h1), .b(adder_3_out), .out(adder_4_out));  // open: cin, cout
  Adder #(.width(16)) adder_5 (.a(16'h1), .b(adder_4_out), .out(adder_5_out));  // open: cin, cout
  Adder #(.width(16)) adder_6 (.a(16'h1), .b(adder_5_out), .out(adder_6_out));  // open: cin, cout
  Adder #(.width(16)) adder_7 (.a(16'h1), .b(adder_6_out), .out(adder_7_out));  // open: cin, cout
  Adder #(.width(16)) adder_8 (.a(16'h1), .b(adder_7_out), .out(CheckCarry));  // open: cin, cout
  Comparator #(.width(16)) comparator_1 (.a(Compared), .b(Check), .eq(A));  // open: gt, lt
  Comparator #(.width(16)) comparator_2 (.a(Compared), .b(adder_1_out), .eq(B));  // open: gt, lt
  Comparator #(.width(16)) comparator_3 (.a(Compared), .b(adder_2_out), .eq(C));  // open: gt, lt
  Comparator #(.width(16)) comparator_4 (.a(Compared), .b(adder_3_out), .eq(D));  // open: gt, lt
  Comparator #(.width(16)) comparator_5 (.a(Compared), .b(adder_4_out), .eq(E));  // open: gt, lt
  Comparator #(.width(16)) comparator_6 (.a(Compared), .b(adder_5_out), .eq(F));  // open: gt, lt
  Comparator #(.width(16)) comparator_7 (.a(Compared), .b(adder_6_out), .eq(G));  // open: gt, lt
  Comparator #(.width(16)) comparator_8 (.a(Compared), .b(adder_7_out), .eq(H));  // open: gt, lt

  assign ComparedCarry = Compared;
endmodule

module KolaR (
  input  Reset
);

  wire brm0_1_programcounterset, clock_1_out;
  wire [15:0] brm0_1_programcounterout, brm0_1_rx, brm0_1_ry, counter_1_q;
  wire [31:0] rom_1_data;

  Clock clock_1 (.out(clock_1_out));
  ROM #(.addrWidth(16), .dataWidth(32)) rom_1 (.addr(counter_1_q), .data(rom_1_data));
  Counter #(.max('hffff), .trigger("falling"), .width(16)) counter_1 (
    .load(brm0_1_programcounterset), .D(brm0_1_programcounterout), .Q(counter_1_q), .clk(clock_1_out),
    .clr(Reset));  // open: count, carry, up
  brm0 brm0_1 (
    .OperationCode(rom_1_data[31:16]), .Operand(rom_1_data[15:0]), .Clock(clock_1_out),
    .ProgramCounter(counter_1_q), .RX(brm0_1_rx), .RY(brm0_1_ry),
    .ProgramCounterOUT(brm0_1_programcounterout), .ProgramCounterSET(brm0_1_programcounterset));
  // LedBar #(.inputtype("row"), .matrixcols(16)) Regx: pin names not known; wires that end beside it: brm0_1_rx
  // LedBar #(.inputtype("row"), .matrixcols(16)) Regy: pin names not known; wires that end beside it: brm0_1_ry

  // Notes on the sheet:
  //   contents of rom_1 (hex, n*v repeats v):
  //   ff 10001 80000 70000 b0001
endmodule
